# Fritzing sketch Nano to RGB Strip (saved by Fritzing 0.9.2b)
breadboards: 1

parts:
  Part1 = Arduino Nano (Rev3.0)
  Q1 = Basic FET N-Channel [package="DPak [SMD]"]
  Q2 = Basic FET N-Channel [package="DPak [SMD]"]
  Q3 = Basic FET N-Channel [package="DPak [SMD]"]
  R1 = Resistor [tolerance=±20% resistance=10k package="0603 [SMD]"]
  R2 = Resistor [tolerance=±20% resistance=10k package="0603 [SMD]"]
  R3 = Resistor [tolerance=±20% resistance=10k package="0603 [SMD]"]

nets:
  N1: Part1.D1/TX, Q1.Gate, Q1.drain
  N2: Part1.D4, R1.Pin_0
  N3: Part1.D5, Q3.drain, Q3.source
  N4: Part1.D7, Q1.source
  N5: Part1.VIN, R2.Pin_0
  N6: Part1.A2, Q2.Gate
  N7: Part1.3V3, R3.Pin_0
  N8: R1.Pin_1, R2.Pin_1
